// Logisim project Lab01.circ as structural Verilog: 1 circuit, main circuit main
module main (
  input  IN1,
  input  IN,
  input  IN_2,
  input  in_4,
  input  A,
  input  A_2,
  input  B,
  input  B_2,
  input  C,
  input  C_2,
  input  D,
  input  D_2,
  input  A_3,
  input  A_4,
  input  B_3,
  input  B_4,
  input  C_3,
  input  C_4,
  input  D_3,
  input  D_4,
  output OUT,
  output OUT_2,
  output out_23,
  output F2,
  output F2_2,
  output F2_3,
  output F2_4
);

  wire A_C_D_2_out, A_C_D_3_out, A_C_D_4_out, A_C_D_out, ACD_2_out, ACD_3_out, ACD_4_out, ACD_out, B_C_2_out,
       B_C_3_out, B_C_4_out, B_C_out, BCD_2_out, BCD_3_out, BCD_4_out, BCD_out, not_2_out, not_3_out,
       not_4_out, not_5_out, not_6_out, not_7_out, not_8_out, not_9_out, not_11_out, not_12_out, not_13_out,
       not_14_out, not_15_out, not_16_out, not_17_out, not_18_out;

  not not_1 (OUT, IN);
  not not_2 (not_2_out, B);
  not not_3 (not_3_out, B_3);
  not not_4 (not_4_out, C);
  not not_5 (not_5_out, D);
  not not_6 (not_6_out, C);
  and BCD (BCD_out, not_2_out, C, D);
  not not_7 (not_7_out, C_3);
  not not_8 (not_8_out, D_3);
  not not_9 (not_9_out, C_3);
  and BCD_2 (BCD_2_out, not_3_out, C_3, D_3);
  and A_C_D (A_C_D_out, A, not_4_out, not_5_out);
  and B_C (B_C_out, B, not_6_out);
  and ACD (ACD_out, A, C, D);
  and A_C_D_2 (A_C_D_2_out, A_3, not_7_out, not_8_out);
  and B_C_2 (B_C_2_out, B_3, not_9_out);
  and ACD_2 (ACD_2_out, A_3, C_3, D_3);
  or u_F2 (F2, A_C_D_out, B_C_out, ACD_out, BCD_out);
  or u_F2_2 (F2_3, A_C_D_2_out, B_C_2_out, ACD_2_out, BCD_2_out);
  not not_10 (OUT_2, IN_2);
  not not_11 (not_11_out, B_2);
  not not_12 (not_12_out, B_4);
  not not_13 (not_13_out, C_2);
  not not_14 (not_14_out, D_2);
  not not_15 (not_15_out, C_2);
  and BCD_3 (BCD_3_out, not_11_out, C_2, D_2);
  not not_16 (not_16_out, C_4);
  not not_17 (not_17_out, D_4);
  not not_18 (not_18_out, C_4);
  and BCD_4 (BCD_4_out, not_12_out, C_4, D_4);
  and A_C_D_3 (A_C_D_3_out, A_2, not_13_out, not_14_out);
  and B_C_3 (B_C_3_out, B_2, not_15_out);
  and ACD_3 (ACD_3_out, A_2, C_2, D_2);
  and A_C_D_4 (A_C_D_4_out, A_4, not_16_out, not_17_out);
  and B_C_4 (B_C_4_out, B_4, not_18_out);
  and ACD_4 (ACD_4_out, A_4, C_4, D_4);
  or or_1 (out_23, IN1, in_4);
  or u_F2_3 (F2_2, A_C_D_3_out, B_C_3_out, ACD_3_out, BCD_3_out);
  or u_F2_4 (F2_4, A_C_D_4_out, B_C_4_out, ACD_4_out, BCD_4_out);
endmodule
