// Logisim project Lab_02.circ as structural Verilog: 1 circuit, main circuit main
// ENABLE
module main (
  input  [7:0] IN,
  input  [7:0] A,
  input  [7:0] B,
  input  [1:0] OPCODE,
  input  ENABLE,
  input  [1:0] Opcode_2,
  output [7:0] Out,
  output [7:0] OUT_2
);

  wire CLOCK_out, decoder_1_out0, decoder_1_out1, decoder_1_out2, decoder_1_out3;
  wire [7:0] adder_1_out, AND_out, NAND_out, register_1_q, register_2_q, register_3_q, register_4_q,
       subtractor_1_out;

  Clock CLOCK (.out(CLOCK_out));
  Decoder #(.select(2)) decoder_1 (
    .out0(decoder_1_out0), .out1(decoder_1_out1), .out2(decoder_1_out2), .out3(decoder_1_out3), .sel(OPCODE),
    .en(ENABLE));
  Register register_1 (.D(IN), .en(decoder_1_out0), .Q(register_1_q), .clk(CLOCK_out));  // open: clr
  Register register_2 (.D(IN), .en(decoder_1_out1), .Q(register_2_q), .clk(CLOCK_out));  // open: clr
  Register register_3 (.D(IN), .en(decoder_1_out2), .Q(register_3_q), .clk(CLOCK_out));  // open: clr
  Register register_4 (.D(IN), .en(decoder_1_out3), .Q(register_4_q), .clk(CLOCK_out));  // open: clr
  Multiplexer #(.select(2), .width(8), .enable("false")) multiplexer_1 (
    .in0(register_1_q), .in1(register_2_q), .in2(register_3_q), .in3(register_4_q), .out(OUT_2), .sel(OPCODE));
  Adder adder_1 (.a(A), .b(B), .out(adder_1_out));  // open: cin, cout
  Subtractor subtractor_1 (.a(A), .b(B), .out(subtractor_1_out));  // open: bin, bout
  assign AND_out = A & B;  // AND_Gate AND, 8 bits wide
  assign NAND_out = ~(A & B);  // NAND_Gate NAND, 8 bits wide
  Multiplexer #(.select(2), .width(8), .enable("false")) multiplexer_2 (
    .in0(adder_1_out), .in1(subtractor_1_out), .in2(AND_out), .in3(NAND_out), .out(Out), .sel(Opcode_2));
endmodule
